// Logisim project Logisim Design.circ as structural Verilog: 17 circuits, main circuit Microprocessor
module Microprocessor (
  input  in_1,
  output out_2,
  output out_3,
  output out_4
);

  wire alu_4bit_1_zf, and_1_out, clock_1_out, controlunit_1_add_sub, controlunit_1_alusrc,
       controlunit_1_branch, controlunit_1_cin, controlunit_1_memtoreg, controlunit_1_mrd, controlunit_1_mwr,
       controlunit_1_regdst, controlunit_1_regwr;
  wire [1:0] mux_2x1_2bit_1_y;
  wire [2:0] controlunit_1_aluop;
  wire [3:0] alu_4bit_1_result, datamemory_16x4_1_readdata, mux_2x1_4bit_1_y, mux_2x1_4bit_2_y,
       programcounter_4bit_1_pcnew, registerfile_16x4_1_readdata1, registerfile_16x4_1_readdata2;
  wire [15:0] instructionmemory_16x16_1_instruction;

  Clock clock_1 (.out(clock_1_out));
  programCounter_4bit programcounter_4bit_1 (
    .PCSrc(and_1_out), .JumpAddress(instructionmemory_16x16_1_instruction[3:0]), .CLK(clock_1_out),
    .CLR(in_1), .PCnew(programcounter_4bit_1_pcnew));
  InstructionMemory_16x16 instructionmemory_16x16_1 (
    .Address(programcounter_4bit_1_pcnew), .Instruction(instructionmemory_16x16_1_instruction));
  RegisterFile_16x4 registerfile_16x4_1 (
    .ReadAdd1(instructionmemory_16x16_1_instruction[11:10]), .WriteAdd(mux_2x1_2bit_1_y),
    .ReadAdd2(instructionmemory_16x16_1_instruction[9:8]), .WriteData(mux_2x1_4bit_2_y),
    .RegWR(controlunit_1_regwr), .CLK(clock_1_out), .CLR(in_1), .ReadData1(registerfile_16x4_1_readdata1),
    .ReadData2(registerfile_16x4_1_readdata2));
  ControlUnit controlunit_1 (
    .Instruction(instructionmemory_16x16_1_instruction[15:12]), .RegWR(controlunit_1_regwr),
    .ALUSrc(controlunit_1_alusrc), .Add_Sub(controlunit_1_add_sub), .Cin(controlunit_1_cin),
    .ALUOp(controlunit_1_aluop), .RegDst(controlunit_1_regdst), .MemtoReg(controlunit_1_memtoreg),
    .MRD(controlunit_1_mrd), .MWR(controlunit_1_mwr), .Branch(controlunit_1_branch));
  ALU_4bit alu_4bit_1 (
    .Add_Sub(controlunit_1_add_sub), .A(registerfile_16x4_1_readdata1), .Cin(controlunit_1_cin),
    .B(mux_2x1_4bit_1_y), .ALUOP(controlunit_1_aluop), .Result(alu_4bit_1_result), .ZF(alu_4bit_1_zf),
    .SF(out_2), .OvF(out_3), .CF(out_4));
  Mux_2x1_4bit mux_2x1_4bit_1 (
    .s(controlunit_1_alusrc), .I1(instructionmemory_16x16_1_instruction[3:0]),
    .I0(registerfile_16x4_1_readdata2), .Y(mux_2x1_4bit_1_y));
  Mux_2x1_2bit mux_2x1_2bit_1 (
    .s(controlunit_1_memtoreg), .I1(instructionmemory_16x16_1_instruction[7:6]),
    .I0(instructionmemory_16x16_1_instruction[9:8]), .Y(mux_2x1_2bit_1_y));
  and and_1 (and_1_out, alu_4bit_1_zf, controlunit_1_branch);
  DataMemory_16x4 datamemory_16x4_1 (
    .CLR(in_1), .Address(alu_4bit_1_result), .MWR(controlunit_1_mwr), .MRD(controlunit_1_mrd),
    .CLK(clock_1_out), .WriteData(registerfile_16x4_1_readdata2), .ReadData(datamemory_16x4_1_readdata));
  Mux_2x1_4bit mux_2x1_4bit_2 (
    .s(controlunit_1_regdst), .I1(datamemory_16x4_1_readdata), .I0(alu_4bit_1_result), .Y(mux_2x1_4bit_2_y));

  // Notes on the sheet:
  //   Simple Microprocessor Design
endmodule

module FullAdder_1bit (
  input  A,
  input  B,
  input  Cin,
  output Sum,
  output Carry
);

  wire halfadder_1bit_1_carry, halfadder_1bit_1_sum, halfadder_1bit_2_carry;

  HalfAdder_1bit halfadder_1bit_1 (.A(A), .B(B), .Sum(halfadder_1bit_1_sum), .Carry(halfadder_1bit_1_carry));
  HalfAdder_1bit halfadder_1bit_2 (.A(halfadder_1bit_1_sum), .B(Cin), .Sum(Sum), .Carry(halfadder_1bit_2_carry));
  or or_1 (Carry, halfadder_1bit_2_carry, halfadder_1bit_1_carry);

  // Notes on the sheet:
  //   Full Adder 1-bit
endmodule

module HalfAdder_1bit (
  input  A,
  input  B,
  output Sum,
  output Carry
);

  xor xor_1 (Sum, A, B);
  and and_1 (Carry, A, B);

  // Notes on the sheet:
  //   Half Adder 1-bit
endmodule

module ALU_1bit (
  input  Binv,
  input  [2:0] ALUop,
  input  A,
  input  B,
  input  Cin,
  input  Less,
  output Result,
  output SET,
  output CF
);

  wire and_1_out, mux_2x1_1bit_1_y, not_1_out, or_1_out;

  not not_1 (not_1_out, B);
  and and_1 (and_1_out, A, B);
  or or_1 (or_1_out, A, B);
  Mux_2x1_1bit mux_2x1_1bit_1 (.s(Binv), .I1(not_1_out), .I0(B), .Y(mux_2x1_1bit_1_y));
  FullAdder_1bit fulladder_1bit_1 (.A(A), .B(mux_2x1_1bit_1_y), .Cin(Cin), .Sum(SET), .Carry(CF));
  Mux_8x1 mux_8x1_1 (
    .S2(ALUop[0]), .S1(ALUop[1]), .S0(ALUop[2]), .I7(1'b0), .I6(1'b0), .I5(1'b0), .I4(1'b0), .I3(Less),
    .I2(SET), .I1(or_1_out), .I0(and_1_out), .Y(Result));

  // Notes on the sheet:
  //   ALU 1-bit
endmodule

module Mux_2x1_1bit (
  input  s,
  input  I1,
  input  I0,
  output Y
);

  wire and_1_out, and_2_out, not_1_out;

  not not_1 (not_1_out, s);
  and and_1 (and_1_out, s, I1);
  and and_2 (and_2_out, not_1_out, I0);
  or or_1 (Y, and_1_out, and_2_out);

  // Notes on the sheet:
  //   Mux 2x1 1-bit
endmodule

module ALU_4bit (
  input  Add_Sub,
  input  [3:0] A,
  input  Cin,
  input  [3:0] B,
  input  [2:0] ALUOP,
  output [3:0] Result,
  output ZF,
  output SF,
  output OvF,
  output CF
);

  wire alu_1bit_1_cf, alu_1bit_2_cf, alu_1bit_3_cf, alu_1bit_4_set;

  ALU_1bit alu_1bit_1 (
    .Binv(Add_Sub), .ALUop(ALUOP), .A(A[0]), .B(B[0]), .Cin(Cin), .Less(alu_1bit_4_set), .Result(Result[0]),
    .CF(alu_1bit_1_cf));  // open: SET
  ALU_1bit alu_1bit_2 (
    .Binv(Add_Sub), .ALUop(ALUOP), .A(A[1]), .B(B[1]), .Cin(alu_1bit_1_cf), .Less(1'b0), .Result(Result[1]),
    .CF(alu_1bit_2_cf));  // open: SET
  ALU_1bit alu_1bit_3 (
    .Binv(Add_Sub), .ALUop(ALUOP), .A(A[2]), .B(B[2]), .Cin(alu_1bit_2_cf), .Less(1'b0), .Result(Result[2]),
    .CF(alu_1bit_3_cf));  // open: SET
  ALU_1bit alu_1bit_4 (
    .Binv(Add_Sub), .ALUop(ALUOP), .A(A[3]), .B(B[3]), .Cin(alu_1bit_3_cf), .Less(1'b0), .Result(Result[3]),
    .SET(alu_1bit_4_set), .CF(CF));
  nor nor_1 (ZF, Result[0], Result[1], Result[2], Result[3]);
  xor xor_1 (OvF, alu_1bit_3_cf, CF);

  assign SF = Result[3];

  // Notes on the sheet:
  //   ALU 4-bit
endmodule

module RegisterFile_16x4 (
  input  [1:0] ReadAdd1,
  input  [1:0] WriteAdd,
  input  [1:0] ReadAdd2,
  input  [3:0] WriteData,
  input  RegWR,
  input  CLK,
  input  CLR,
  output [3:0] ReadData1,
  output [3:0] ReadData2
);

  wire and_1_out, and_2_out, and_3_out, and_4_out, decoder_1x4_1_y0, decoder_1x4_1_y1, decoder_1x4_1_y2,
       decoder_1x4_1_y3;
  wire [3:0] register_1_q, register_2_q, register_3_q, register_4_q;

  Decoder_1x4 decoder_1x4_1 (
    .A(WriteAdd[1]), .B(WriteAdd[0]), .E(RegWR), .Y0(decoder_1x4_1_y0), .Y1(decoder_1x4_1_y1),
    .Y2(decoder_1x4_1_y2), .Y3(decoder_1x4_1_y3));
  Register #(.trigger("falling"), .width(4)) register_1 (
    .D(WriteData), .en(and_1_out), .clk(CLK), .Q(register_1_q), .clr(CLR));
  and and_1 (and_1_out, decoder_1x4_1_y0, RegWR);
  Register #(.trigger("falling"), .width(4)) register_2 (
    .D(WriteData), .en(and_2_out), .clk(CLK), .Q(register_2_q), .clr(CLR));
  and and_2 (and_2_out, decoder_1x4_1_y1, RegWR);
  Register #(.trigger("falling"), .width(4)) register_3 (
    .D(WriteData), .en(and_3_out), .clk(CLK), .Q(register_3_q), .clr(CLR));
  and and_3 (and_3_out, decoder_1x4_1_y2, RegWR);
  Register #(.trigger("falling"), .width(4)) register_4 (
    .D(WriteData), .en(and_4_out), .clk(CLK), .Q(register_4_q), .clr(CLR));
  and and_4 (and_4_out, decoder_1x4_1_y3, RegWR);
  Mux_4x1_4bit mux_4x1_4bit_1 (
    .S1(ReadAdd1[1]), .I3(register_4_q), .S0(ReadAdd1[0]), .I2(register_3_q), .I1(register_2_q),
    .I0(register_1_q), .Y(ReadData1));
  Mux_4x1_4bit mux_4x1_4bit_2 (
    .S1(ReadAdd2[1]), .I3(register_4_q), .S0(ReadAdd2[0]), .I2(register_3_q), .I1(register_2_q),
    .I0(register_1_q), .Y(ReadData2));

  // Notes on the sheet:
  //   RF 16x4
endmodule

module Decoder_1x4 (
  input  A,
  input  B,
  input  E,
  output Y0,
  output Y1,
  output Y2,
  output Y3
);

  wire not_1_out, not_2_out;

  not not_1 (not_1_out, A);
  not not_2 (not_2_out, B);
  and and_1 (Y0, not_1_out, not_2_out, E);
  and and_2 (Y1, not_1_out, B, E);
  and and_3 (Y2, A, not_2_out, E);
  and and_4 (Y3, A, B, E);

  // Notes on the sheet:
  //   Dec 1x4 1-bit
endmodule

module Mux_4x1_4bit (
  input  S1,
  input  [3:0] I3,
  input  S0,
  input  [3:0] I2,
  input  [3:0] I1,
  input  [3:0] I0,
  output [3:0] Y
);

  wire [3:0] and_1_out, and_2_out, and_3_out, and_4_out, not_1_out, not_2_out;

  assign not_1_out = ~{4{S1}};  // NOT_Gate not_1, 4 bits wide
  assign not_2_out = ~{4{S0}};  // NOT_Gate not_2, 4 bits wide
  assign and_1_out = {4{S1}} & {4{S0}} & I3;  // AND_Gate and_1, 4 bits wide
  assign and_2_out = {4{S1}} & not_2_out & I2;  // AND_Gate and_2, 4 bits wide
  assign and_3_out = not_1_out & {4{S0}} & I1;  // AND_Gate and_3, 4 bits wide
  assign and_4_out = not_1_out & not_2_out & I0;  // AND_Gate and_4, 4 bits wide
  assign Y = and_1_out | and_2_out | and_3_out | and_4_out;  // OR_Gate or_1, 4 bits wide

  // Notes on the sheet:
  //   Mux 4x1 4-bit
endmodule

module InstructionMemory_16x16 (
  input  [3:0] Address,
  output [15:0] Instruction
);

  ROM #(.addrWidth(4), .dataWidth(16)) rom_1 (.addr(Address), .data(Instruction));

  // Notes on the sheet:
  //   contents of rom_1 (hex, n*v repeats v):
  //   6405
  //   IM 16x16
endmodule

module DataMemory_16x4 (
  input  CLR,
  input  [3:0] Address,
  input  MWR,
  input  MRD,
  input  CLK,
  input  [3:0] WriteData,
  output [3:0] ReadData
);

  wire not_1_out;

  not not_1 (not_1_out, CLR);
  RAM #(.addrWidth(4), .asyncread("true"), .clearpin("true"), .dataWidth(4)) ram_1 (
    .addr(Address), .we(MWR), .oe(MRD), .clk(CLK), .din(WriteData), .dout(ReadData), .clr(not_1_out));

  // Notes on the sheet:
  //   DM 16x4
endmodule

module Mux_8x1 (
  input  S2,
  input  S1,
  input  S0,
  input  I7,
  input  I6,
  input  I5,
  input  I4,
  input  I3,
  input  I2,
  input  I1,
  input  I0,
  output Y
);

  wire and_1_out, and_2_out, and_3_out, and_4_out, and_5_out, and_6_out, and_7_out, and_8_out, not_1_out,
       not_2_out, not_3_out;

  not not_1 (not_1_out, S2);
  not not_2 (not_2_out, S1);
  not not_3 (not_3_out, S0);
  and and_1 (and_1_out, S2, S1, S0, I7);
  and and_2 (and_2_out, not_1_out, S1, S0, I6);
  and and_3 (and_3_out, S2, not_2_out, S0, I5);
  and and_4 (and_4_out, not_1_out, not_2_out, S0, I4);
  and and_5 (and_5_out, S2, S1, not_3_out, I3);
  and and_6 (and_6_out, not_1_out, S1, not_3_out, I2);
  and and_7 (and_7_out, S2, not_2_out, not_3_out, I1);
  and and_8 (and_8_out, not_1_out, not_2_out, not_3_out, I0);
  or or_1 (Y, and_1_out, and_2_out, and_3_out, and_4_out, and_5_out, and_6_out, and_7_out, and_8_out);

  // Notes on the sheet:
  //   Mux 8x1 1-bit
endmodule

module programCounter_4bit (
  input  PCSrc,
  input  [3:0] JumpAddress,
  input  CLK,
  input  CLR,
  output [3:0] PCnew
);

  wire not_1_out;
  wire [3:0] fulladder_4bit_1_sum, mux_2x1_4bit_1_y;

  Mux_2x1_4bit mux_2x1_4bit_1 (.s(PCSrc), .I1(JumpAddress), .I0(fulladder_4bit_1_sum), .Y(mux_2x1_4bit_1_y));
  not not_1 (not_1_out, CLK);
  Register #(.width(4)) register_1 (.D(mux_2x1_4bit_1_y), .en(1'b1), .clk(not_1_out), .Q(PCnew), .clr(CLR));
  Fulladder_4bit fulladder_4bit_1 (.A(4'b0001), .B(PCnew), .Sum(fulladder_4bit_1_sum));  // open: Cin, Cout

  // Notes on the sheet:
  //   PC 4-bit
endmodule

module Fulladder_4bit (
  input  [3:0] A,
  input  Cin,
  input  [3:0] B,
  output [3:0] Sum,
  output Cout
);

  wire fulladder_1bit_1_carry, fulladder_1bit_2_carry, fulladder_1bit_3_carry;

  FullAdder_1bit fulladder_1bit_1 (.A(A[0]), .B(B[0]), .Cin(Cin), .Sum(Sum[0]), .Carry(fulladder_1bit_1_carry));
  FullAdder_1bit fulladder_1bit_2 (
    .A(A[1]), .B(B[1]), .Cin(fulladder_1bit_1_carry), .Sum(Sum[1]), .Carry(fulladder_1bit_2_carry));
  FullAdder_1bit fulladder_1bit_3 (
    .A(A[2]), .B(B[2]), .Cin(fulladder_1bit_2_carry), .Sum(Sum[2]), .Carry(fulladder_1bit_3_carry));
  FullAdder_1bit fulladder_1bit_4 (.A(A[3]), .B(B[3]), .Cin(fulladder_1bit_3_carry), .Sum(Sum[3]), .Carry(Cout));

  // Notes on the sheet:
  //   Full Adder 4-bit
endmodule

module ControlUnit (
  input  [3:0] Instruction,
  output RegWR,
  output ALUSrc,
  output Add_Sub,
  output Cin,
  output [2:0] ALUOp,
  output RegDst,
  output MemtoReg,
  output MRD,
  output MWR,
  output Branch
);

  wire decoder_1_out0, decoder_1_out1, decoder_1_out2, decoder_1_out3, decoder_1_out4, decoder_1_out5,
       decoder_1_out6, decoder_1_out7, decoder_1_out8, decoder_1_out9, decoder_1_out10, decoder_1_out11;

  Decoder #(.enable("false"), .select(4)) decoder_1 (
    .out0(decoder_1_out0), .out1(decoder_1_out1), .out2(decoder_1_out2), .out3(decoder_1_out3),
    .out4(decoder_1_out4), .out5(decoder_1_out5), .out6(decoder_1_out6), .out7(decoder_1_out7),
    .out8(decoder_1_out8), .out9(decoder_1_out9), .out10(decoder_1_out10), .out11(decoder_1_out11),
    .out14(MemtoReg), .out15(MWR), .sel(Instruction));  // open: out12, out13
  or or_1 (RegWR, decoder_1_out0, decoder_1_out1, decoder_1_out2, decoder_1_out3, decoder_1_out4, decoder_1_out5, decoder_1_out6, decoder_1_out7, decoder_1_out8, decoder_1_out9, MemtoReg);
  or or_2 (ALUSrc, decoder_1_out10, decoder_1_out4, decoder_1_out5, decoder_1_out6, decoder_1_out7, decoder_1_out9, MemtoReg, MWR, decoder_1_out11);
  or or_3 (Add_Sub, decoder_1_out3, decoder_1_out7, decoder_1_out8, decoder_1_out9, decoder_1_out10, decoder_1_out11, MemtoReg, MWR);
  or or_4 (Cin, decoder_1_out3, decoder_1_out7, decoder_1_out8, decoder_1_out9, decoder_1_out10, decoder_1_out11);
  or or_5 (ALUOp[1], decoder_1_out8, decoder_1_out2, decoder_1_out3, decoder_1_out6, decoder_1_out7, decoder_1_out10, decoder_1_out11, MemtoReg, MWR, decoder_1_out9);
  or or_6 (ALUOp[0], decoder_1_out1, decoder_1_out5, decoder_1_out8, decoder_1_out9);
  or or_7 (Branch, decoder_1_out10, decoder_1_out11);

  assign ALUOp[2] = 1'b0;
  assign MRD = MemtoReg;
  assign RegDst = MemtoReg;

  // Notes on the sheet:
  //   Control Unit
endmodule

module Mux_2x1_2bit (
  input  s,
  input  [1:0] I1,
  input  [1:0] I0,
  output [1:0] Y
);

  wire [1:0] and_1_out, and_2_out, not_1_out;

  assign not_1_out = ~{2{s}};  // NOT_Gate not_1, 2 bits wide
  assign and_1_out = {2{s}} & I1;  // AND_Gate and_1, 2 bits wide
  assign and_2_out = not_1_out & I0;  // AND_Gate and_2, 2 bits wide
  assign Y = and_1_out | and_2_out;  // OR_Gate or_1, 2 bits wide

  // Notes on the sheet:
  //   Mux 2x1 2-bit
endmodule

module Mux_2x1_4bit (
  input  s,
  input  [3:0] I1,
  input  [3:0] I0,
  output [3:0] Y
);

  wire [3:0] and_1_out, and_2_out, not_1_out;

  assign not_1_out = ~{4{s}};  // NOT_Gate not_1, 4 bits wide
  assign and_1_out = {4{s}} & I1;  // AND_Gate and_1, 4 bits wide
  assign and_2_out = not_1_out & I0;  // AND_Gate and_2, 4 bits wide
  assign Y = and_1_out | and_2_out;  // OR_Gate or_1, 4 bits wide

  // Notes on the sheet:
  //   Mux 2x1 4-bit
endmodule
